# Fritzing sketch KFBot (saved by Fritzing 0.9.5d)
breadboards: 2

parts:
  元件1 = Arduino Uno (Rev3)
  LCD1 = LCD screen
  元件2 = Bluetooth HC-05 Macho
  R1 = Resistor [tolerance=±5% resistance=10000 package=THT]
  S1 = Pushbutton [package="[SMD]"]
  S2 = Pushbutton [package="[SMD]"]
  S3 = Pushbutton [package="[SMD]"]
  S4 = Pushbutton [package="[SMD]"]
  R2 = Resistor [tolerance=±5% resistance=10000 package=THT]
  R3 = Resistor [tolerance=±5% resistance=10000 package=THT]
  R4 = Resistor [tolerance=±5% resistance=10000 package=THT]
  R5 = Resistor [tolerance=±5% resistance=10000 package=THT]
  R6 = Resistor [tolerance=±5% resistance=20000 package=THT]
  R7 = Resistor [tolerance=±5% resistance=680 package=THT]
  R8 = Resistor [tolerance=±5% resistance=200 package=THT]
  R9 = Resistor [tolerance=±5% resistance=330 package=THT]

nets:
  N1: 元件1.A0, R1.Pin_0, S1.Pin_1, S1.Pin_2
  N2: 元件1.A1, S2.Pin_1, S2.Pin_2, R2.Pin_0
  N3: 元件1.A2, S3.Pin_1, S3.Pin_2, R3.Pin_0
  N4: 元件1.D8, LCD1.E
  N5: 元件1.D9_PWM, LCD1.RS
  N6: 元件1.D10_PWM/SS, 元件2.TXD
  N7: 元件1.D11_PWM/MOSI, R5.Pin_0
  N8: 元件1.D3_PWM, S4.Pin_1, S4.Pin_2, R4.Pin_0
  N9: 元件1.D4, LCD1.DB7
  N10: 元件1.D5_PWM, LCD1.DB6
  N11: 元件1.D6_PWM, LCD1.DB5
  N12: 元件1.D7, LCD1.DB4
  5V: 元件1.5V, LCD1.VDD, 元件2.VCC, R1.Pin_1, R2.Pin_1, R3.Pin_1, R4.Pin_1, R7.Pin_0, R9.Pin_1
  GND: 元件1.GND, LCD1.VSS, LCD1.R/W, LCD1.LED-, 元件2.GND, S1.Pin_3, S1.Pin_4, S2.Pin_3, S2.Pin_4, S3.Pin_3, S3.Pin_4, S4.Pin_3, S4.Pin_4, R6.Pin_1, R8.Pin_0
  N13: LCD1.V0, R7.Pin_1, R8.Pin_1
  N14: LCD1.LED+, R9.Pin_0
  N15: 元件2.RXD, R5.Pin_1, R6.Pin_0

notes:
  680Ω
  四个电阻均为10kΩ
  200Ω
  20kΩ
  10kΩ
  330Ω
